# Fritzing sketch Untitled Sketch 2 (saved by Fritzing 1.0.1rc)
breadboards: 1

parts:
  Part2 = Arduino Mega 2560 (Rev3)
  U2 = NodeMCU V1.0
  LED14 = smd LED [color="Yellow (595nm)" package="0603 [SMD]"]
  LED15 = smd LED [color="Yellow (595nm)" package="0603 [SMD]"]
  LED16 = smd LED [color="Yellow (595nm)" package="0603 [SMD]"]
  LED17 = smd LED [color="Yellow (595nm)" package="0603 [SMD]"]
  LED18 = smd LED [color="Yellow (595nm)" package="0603 [SMD]"]
  LED6_تقاطع1 = smd LED [color="Yellow (595nm)" package="0603 [SMD]"]
  LED19 = smd LED [color="Yellow (595nm)" package="0603 [SMD]"]
  LED5_تقاطع1 = smd LED [color="Yellow (595nm)" package="0603 [SMD]"]
  LED4_تقاطع1 = smd LED [color="Yellow (595nm)" package="0603 [SMD]"]
  LED3_تقاطع1 = smd LED [color="Yellow (595nm)" package="0603 [SMD]"]
  LED2_تقاطع1 = smd LED [color="Yellow (595nm)" package="0603 [SMD]"]
  LED1_تقاطع_1 = smd LED [color="Yellow (595nm)" package="0603 [SMD]"]
  R15_10K_ohm1 = Resistor [tolerance=±5% resistance=10k power=0.25W package=THT]
  R27 = Photocell (LDR) [package=THT]
  M9_تقاطع_1 = fc-51 [package=THT]
  M8_تقاطع1 = fc-51 [package=THT]
  M8 = fc-51 [package=THT]
  M6_تقاطع1 = fc-51 [package=THT]
  M9 = fc-51 [package=THT]
  M10 = fc-51 [package=THT]
  M11 = fc-51 [package=THT]
  M12 = fc-51 [package=THT]
  M13 = fc-51 [package=THT]

nets:
  N1: Part2.A0, R15_10K_ohm1.Pin_1, R27.pin_0
  N2: Part2.D13_PWM, LED15.cathode
  N3: Part2.D12_PWM, LED17.cathode
  N4: Part2.D11_PWM, LED14.cathode
  N5: Part2.D10_PWM, LED16.cathode
  N6: Part2.D9_PWM, LED6_تقاطع1.cathode
  N7: Part2.D8_PWM, LED5_تقاطع1.cathode
  N8: Part2.D2_PWM, LED4_تقاطع1.cathode
  N9: Part2.D3_PWM, LED3_تقاطع1.cathode
  N10: Part2.D4_PWM, LED2_تقاطع1.cathode
  N11: Part2.D5_PWM, LED1_تقاطع_1.cathode
  N12: Part2.D6_PWM, LED18.cathode
  N13: Part2.D7_PWM, LED19.cathode
  N14: Part2.D23, M9_تقاطع_1.pin1
  N15: Part2.D25, M8_تقاطع1.pin1
  N16: Part2.D27, M6_تقاطع1.pin1
  N17: Part2.D29, M10.pin1
  N18: Part2.D31, M9.pin1
  N19: Part2.D33, M8.pin1
  N20: Part2.D35, M11.pin1
  N21: Part2.D37, M12.pin1
  N22: Part2.D39, M13.pin1
  N23: Part2.D45, U2.D6
  N24: Part2.D47, U2.D5
  N25: Part2.D49, U2.D4
  N26: Part2.D51, U2.D3
  N27: Part2.D53, U2.D0
  N28: U2.3V3, R27.pin_1, M9_تقاطع_1.pin3, M8_تقاطع1.pin3, M8.pin2, M8.pin3, M6_تقاطع1.pin3, M9.pin3, M10.pin3, M11.pin3, M12.pin3, M13.pin3
  N29: U2.GND, LED14.anode, LED15.anode, LED16.anode, LED17.anode, LED18.anode, LED6_تقاطع1.anode, LED19.anode, LED5_تقاطع1.anode, LED4_تقاطع1.anode, LED3_تقاطع1.anode, LED2_تقاطع1.anode, LED1_تقاطع_1.anode, R15_10K_ohm1.Pin_0, M9_تقاطع_1.pin2, M8_تقاطع1.pin2, M6_تقاطع1.pin2, M9.pin2, M10.pin2, M11.pin2, M12.pin2, M13.pin2

custom parts:
  NodeMCU V1.0: ESP8266 based NodeMCU
